// Logisim project g2.circ as structural Verilog: 15 circuits, main circuit CPU
module _1_bit_sum (
  input  cin,
  input  a,
  input  b,
  output out_4
);

  wire and_1_out, and_2_out, and_3_out, and_4_out;

  and and_1 (and_1_out, ~cin, a, ~b);  // AND_Gate
  and and_2 (and_2_out, ~cin, ~a, b);  // AND_Gate
  and and_3 (and_3_out, cin, ~a, ~b);  // AND_Gate
  and and_4 (and_4_out, cin, a, b);
  or or_1 (out_4, and_1_out, and_2_out, and_3_out, and_4_out);
endmodule

module _1_bit_carryout (
  input  cin,
  input  a,
  input  b,
  output out_4
);

  wire and_1_out, and_2_out, and_3_out;

  and and_1 (and_1_out, cin, a);
  and and_2 (and_2_out, cin, b);
  and and_3 (and_3_out, a, b);
  or or_1 (out_4, and_1_out, and_2_out, and_3_out);
endmodule

module _1_bit_full_adder (
  input  cin,
  input  a,
  input  b,
  output sum,
  output cout
);

  _1_bit_sum u_1_bit_sum_1 (.cin(cin), .a(a), .b(b), .out_4(sum));
  _1_bit_carryout u_1_bit_carryout_1 (.cin(cin), .a(a), .b(b), .out_4(cout));
endmodule

module _1_bit_ALU (
  input  ainvert,
  input  binvert,
  input  cin,
  input  [1:0] op,
  input  a,
  input  b,
  input  less,
  output result,
  output cout
);

  wire and_1_out, multiplexer_1_out, multiplexer_2_out, n1_bit_full_adder_1_sum, not_1_out, not_2_out,
       or_1_out;

  Multiplexer multiplexer_1 (.in0(a), .in1(not_1_out), .out(multiplexer_1_out), .sel(ainvert));
  not not_1 (not_1_out, a);
  not not_2 (not_2_out, b);
  Multiplexer multiplexer_2 (.in0(b), .in1(not_2_out), .out(multiplexer_2_out), .sel(binvert));
  and and_1 (and_1_out, multiplexer_1_out, multiplexer_2_out);
  or or_1 (or_1_out, multiplexer_1_out, multiplexer_2_out);
  _1_bit_full_adder u_1_bit_full_adder_1 (
    .a(multiplexer_1_out), .b(multiplexer_2_out), .cin(cin), .cout(cout), .sum(n1_bit_full_adder_1_sum));
  Multiplexer #(.select(2)) multiplexer_3 (
    .in0(and_1_out), .in1(or_1_out), .in2(n1_bit_full_adder_1_sum), .in3(less), .out(result), .sel(op));
endmodule

module Overflow_detection (
  input  cin,
  input  cout,
  output Overflow
);

  wire and_1_out, and_2_out;

  and and_1 (and_1_out, ~cin, cout);  // AND_Gate
  and and_2 (and_2_out, cin, ~cout);  // AND_Gate
  or or_1 (Overflow, and_1_out, and_2_out);
endmodule

module _1_bit_ALU_overflow_detect (
  input  ainvert,
  input  binvert,
  input  cin,
  input  [1:0] op,
  input  a,
  input  b,
  input  less,
  output result,
  output set,
  output Overflow
);

  wire and_1_out, multiplexer_1_out, multiplexer_2_out, n1_bit_full_adder_1_cout, not_1_out, not_2_out,
       or_1_out;

  Multiplexer multiplexer_1 (.in0(a), .in1(not_1_out), .out(multiplexer_1_out), .sel(ainvert));
  not not_1 (not_1_out, a);
  not not_2 (not_2_out, b);
  Multiplexer multiplexer_2 (.in0(b), .in1(not_2_out), .out(multiplexer_2_out), .sel(binvert));
  and and_1 (and_1_out, multiplexer_1_out, multiplexer_2_out);
  or or_1 (or_1_out, multiplexer_1_out, multiplexer_2_out);
  _1_bit_full_adder u_1_bit_full_adder_1 (
    .a(multiplexer_1_out), .b(multiplexer_2_out), .cin(cin), .cout(n1_bit_full_adder_1_cout), .sum(set));
  Overflow_detection overflow_detection_1 (.cin(cin), .cout(n1_bit_full_adder_1_cout), .Overflow(Overflow));
  Multiplexer #(.select(2)) multiplexer_3 (
    .in0(and_1_out), .in1(or_1_out), .in2(set), .in3(less), .out(result), .sel(op));
endmodule

module _4_bit_ALU (
  input  [3:0] Control,
  input  [3:0] a,
  input  [3:0] b,
  output [3:0] result,
  output Zero,
  output Overflow
);

  wire n1_bit_alu_1_cout, n1_bit_alu_2_cout, n1_bit_alu_3_cout, n1_bit_alu_overflow_detect_1_set, or_1_out;

  _1_bit_ALU u_1_bit_alu_1 (
    .a(a[0]), .b(b[0]), .less(n1_bit_alu_overflow_detect_1_set), .ainvert(Control[3]), .binvert(Control[2]),
    .cin(Control[2]), .op(Control[1:0]), .cout(n1_bit_alu_1_cout), .result(result[0]));
  _1_bit_ALU u_1_bit_alu_2 (
    .a(a[1]), .b(b[1]), .less(1'b0), .ainvert(Control[3]), .binvert(Control[2]), .cin(n1_bit_alu_1_cout),
    .op(Control[1:0]), .cout(n1_bit_alu_2_cout), .result(result[1]));
  _1_bit_ALU u_1_bit_alu_3 (
    .a(a[2]), .b(b[2]), .less(1'b0), .ainvert(Control[3]), .binvert(Control[2]), .cin(n1_bit_alu_2_cout),
    .op(Control[1:0]), .cout(n1_bit_alu_3_cout), .result(result[2]));
  _1_bit_ALU_overflow_detect u_1_bit_alu_overflow_detect_1 (
    .a(a[3]), .b(b[3]), .less(1'b0), .ainvert(Control[3]), .binvert(Control[2]), .cin(n1_bit_alu_3_cout),
    .op(Control[1:0]), .result(result[3]), .set(n1_bit_alu_overflow_detect_1_set), .Overflow(Overflow));
  not not_1 (Zero, or_1_out);
  or or_1 (or_1_out, result[0], result[1], result[2], result[3]);
endmodule

module _16_32_bit_extender (
  input  SignExtend,
  input  [15:0] in,
  output [31:0] out
);

  Multiplexer #(.width(32)) multiplexer_1 (
    .in0({{16{1'b0}}, in}), .in1({{17{in[15]}}, in[14:0]}), .out(out), .sel(SignExtend));
endmodule

module Control (
  input  [5:0] Instruction_input,
  output SignExtend,
  output [1:0] WB,
  output [2:0] M,
  output [6:0] EX
);

  PLA #(.in_width(6), .out_width(9), .truth_table("000000,010010001#R-instructions\n001001,101010000#addiu\n00110x,001010000#andi/ori\n000100,100000010#beq\n101011,001000100#sw\n100011,001111000#lw\n001010,101010000#slti")) pla_1 (.out(M));  // open: in
  PLA #(.in_width(6), .out_width(4), .truth_table("001001,0010#addiu\n001100,0000#andi\n001101,0001#ori\n001010,0111#slti\n10x011,0010#sw og lw\n000100,0110#beq")) pla_2 (.out(EX[6:3]));  // open: in
endmodule

module ALU_Control (
  input  [3:0] immidiate_input,
  input  [5:0] funct,
  input  ALUOp_in,
  output [3:0] ALU_input
);

  wire [3:0] pla_1_p1;

  // PLA #(.in_width(6), .out_width(4), .truth_table("100001,0010#addu\n100011,0110#subu\n100100,0000#and\n100101,0001#or\n101010,0111#slt")) pla_1: pin names not known; wires that end beside it: pla_1_p1
  Multiplexer #(.width(4)) multiplexer_1 (.in0(immidiate_input), .in1(pla_1_p1), .out(ALU_input), .sel(ALUOp_in));
endmodule

module CPU (
);

  wire and_1_out, clock_1_out, control_1_signextend, ex_mem_1_zero_output, mips_alu_1_p4;
  wire [1:0] control_1_wb, ex_mem_1_wb_output, id_ex_1_wb_output, registerfile_1_p3;
  wire [2:0] control_1_m, ex_mem_1_m_output, id_ex_1_m_output;
  wire [3:0] alu_control_1_alu_input;
  wire [4:0] ex_mem_1_regdst_output, id_ex_1_rd_output, id_ex_1_rt_output, multiplexer_2_out,
       registerfile_1_p4;
  wire [6:0] control_1_ex, id_ex_1_ex_output;
  wire [31:0] adder_1_out, adder_2_out, ex_mem_1_alu_res_output, ex_mem_1_pc_output,
       ex_mem_1_read_data2_output, id_ex_1_pc_output, id_ex_1_read_data1_output, id_ex_1_read_data2_output,
       id_ex_1_signextend_output, if_id_1_instruction_output, if_id_1_pc_output, mem_wb_1_address_output,
       mem_wb_1_read_data_output, mips_alu_1_p5, mips_ram_1_p6, mipsprogramrom_1_p2, multiplexer_1_out,
       multiplexer_3_out, n16_32_bit_extender_1_out, register_1_q, registerfile_1_p1, registerfile_1_p7,
       registerfile_1_p8, shifter_1_out;

  Multiplexer #(.width(32)) multiplexer_1 (
    .in0(adder_1_out), .in1(ex_mem_1_pc_output), .out(multiplexer_1_out), .sel(and_1_out));
  Register #(.width(32)) register_1 (
    .D(multiplexer_1_out), .en(1'b1), .Q(register_1_q), .clk(clock_1_out));  // open: clr
  Clock clock_1 (.out(clock_1_out));
  Adder #(.width(32)) adder_1 (.a(register_1_q), .b(32'h4), .out(adder_1_out));  // open: cin, cout
  // MIPSProgramROM mipsprogramrom_1: pin names not known; wires that end beside it: register_1_q, mipsprogramrom_1_p2
  IF_ID if_id_1 (
    .PC_input(adder_1_out), .Instruction_input(mipsprogramrom_1_p2), .Clock(clock_1_out),
    .PC_output(if_id_1_pc_output), .Instruction_output(if_id_1_instruction_output));
  Control control_1 (
    .Instruction_input(if_id_1_instruction_output[31:26]), .SignExtend(control_1_signextend),
    .WB(control_1_wb), .M(control_1_m), .EX(control_1_ex));
  _16_32_bit_extender u_16_32_bit_extender_1 (
    .in(if_id_1_instruction_output[15:0]), .SignExtend(control_1_signextend), .out(n16_32_bit_extender_1_out));
  // RegisterFile registerfile_1: pin names not known; wires that end beside it: registerfile_1_p1, clock_1_out, registerfile_1_p3[0], registerfile_1_p4, if_id_1_instruction_output[25:21], if_id_1_instruction_output[20:16], registerfile_1_p7, registerfile_1_p8
  ID_EX id_ex_1 (
    .WB_input(control_1_wb), .M_input(control_1_m), .EX_input(control_1_ex), .PC_input(if_id_1_pc_output),
    .Read_Data1_input(registerfile_1_p7), .Read_Data2_input(registerfile_1_p8),
    .Signextend_input(n16_32_bit_extender_1_out), .rt_input(if_id_1_instruction_output[20:16]),
    .rd_input(if_id_1_instruction_output[15:11]), .Clock(clock_1_out), .WB_output(id_ex_1_wb_output),
    .M_output(id_ex_1_m_output), .EX_output(id_ex_1_ex_output), .PC_output(id_ex_1_pc_output),
    .Read_Data1_output(id_ex_1_read_data1_output), .Read_Data2_output(id_ex_1_read_data2_output),
    .Signextend_output(id_ex_1_signextend_output), .rt_output(id_ex_1_rt_output),
    .rd_output(id_ex_1_rd_output));
  ALU_Control alu_control_1 (
    .funct(id_ex_1_signextend_output[5:0]), .ALUOp_in(id_ex_1_ex_output[0]),
    .immidiate_input(id_ex_1_ex_output[6:3]), .ALU_input(alu_control_1_alu_input));
  Multiplexer #(.width(5)) multiplexer_2 (
    .in0(id_ex_1_rt_output), .in1(id_ex_1_rd_output), .out(multiplexer_2_out), .sel(id_ex_1_ex_output[2]));
  Multiplexer #(.width(32)) multiplexer_3 (
    .in0(id_ex_1_read_data2_output), .in1(id_ex_1_signextend_output), .out(multiplexer_3_out),
    .sel(id_ex_1_ex_output[1]));
  Shifter #(.width(32)) shifter_1 (.in(id_ex_1_signextend_output), .\dist (5'b00010), .out(shifter_1_out));
  Adder #(.width(32)) adder_2 (.a(id_ex_1_pc_output), .b(shifter_1_out), .out(adder_2_out));  // open: cin, cout
  // Mips_ALU mips_alu_1: pin names not known; wires that end beside it: id_ex_1_read_data1_output, multiplexer_3_out, alu_control_1_alu_input, mips_alu_1_p4, mips_alu_1_p5
  EX_MEM ex_mem_1 (
    .WB_input(id_ex_1_wb_output), .M_input(id_ex_1_m_output), .PC_input(adder_2_out),
    .Zero_input(mips_alu_1_p4), .ALU_res_input(mips_alu_1_p5), .Read_Data2_input(id_ex_1_read_data2_output),
    .RegDst_input(multiplexer_2_out), .Clock(clock_1_out), .WB_output(ex_mem_1_wb_output),
    .M_output(ex_mem_1_m_output), .PC_output(ex_mem_1_pc_output), .Zero_output(ex_mem_1_zero_output),
    .ALU_res_output(ex_mem_1_alu_res_output), .Read_Data2_output(ex_mem_1_read_data2_output),
    .RegDst_output(ex_mem_1_regdst_output));
  and and_1 (and_1_out, ex_mem_1_m_output[0], ex_mem_1_zero_output);
  // MIPS_RAM #(.addrWidth(24)) mips_ram_1: pin names not known; wires that end beside it: ex_mem_1_alu_res_output[23:0], ex_mem_1_read_data2_output, ex_mem_1_m_output[1], ex_mem_1_m_output[2], clock_1_out, mips_ram_1_p6
  MEM_WB mem_wb_1 (
    .WB_input(ex_mem_1_wb_output), .Read_Data_input(mips_ram_1_p6), .Address_input(ex_mem_1_alu_res_output),
    .RegDst_input(ex_mem_1_regdst_output), .Clock(clock_1_out), .WB_output(registerfile_1_p3),
    .Read_Data_output(mem_wb_1_read_data_output), .Address_output(mem_wb_1_address_output),
    .RegDst_output(registerfile_1_p4));
  Multiplexer #(.width(32)) multiplexer_4 (
    .in0(mem_wb_1_address_output), .in1(mem_wb_1_read_data_output), .out(registerfile_1_p1),
    .sel(registerfile_1_p3[1]));
endmodule

module IF_ID (
  input  [31:0] PC_input,
  input  [31:0] Instruction_input,
  input  Clock,
  output [31:0] PC_output,
  output [31:0] Instruction_output
);

  Register #(.width(32)) register_1 (.D(PC_input), .Q(PC_output), .clk(Clock));  // open: en, clr
  Register #(.width(32)) register_2 (.D(Instruction_input), .Q(Instruction_output), .clk(Clock));  // open: en, clr
endmodule

module ID_EX (
  input  [1:0] WB_input,
  input  [2:0] M_input,
  input  [6:0] EX_input,
  input  [31:0] PC_input,
  input  [31:0] Read_Data1_input,
  input  [31:0] Read_Data2_input,
  input  [31:0] Signextend_input,
  input  [4:0] rt_input,
  input  [4:0] rd_input,
  input  Clock,
  output [1:0] WB_output,
  output [2:0] M_output,
  output [6:0] EX_output,
  output [31:0] PC_output,
  output [31:0] Read_Data1_output,
  output [31:0] Read_Data2_output,
  output [31:0] Signextend_output,
  output [4:0] rt_output,
  output [4:0] rd_output
);

  Register #(.width(2)) register_1 (.D(WB_input), .Q(WB_output), .clk(Clock));  // open: en, clr
  Register #(.width(3)) register_2 (.D(M_input), .Q(M_output), .clk(Clock));  // open: en, clr
  Register #(.width(7)) register_3 (.D(EX_input), .Q(EX_output), .clk(Clock));  // open: en, clr
  Register #(.width(32)) register_4 (.D(PC_input), .Q(PC_output), .clk(Clock));  // open: en, clr
  Register #(.width(32)) register_5 (.D(Read_Data1_input), .Q(Read_Data1_output), .clk(Clock));  // open: en, clr
  Register #(.width(32)) register_6 (.D(Read_Data2_input), .Q(Read_Data2_output), .clk(Clock));  // open: en, clr
  Register #(.width(32)) register_7 (.D(Signextend_input), .Q(Signextend_output), .clk(Clock));  // open: en, clr
  Register #(.width(5)) register_8 (.D(rt_input), .Q(rt_output), .clk(Clock));  // open: en, clr
  Register #(.width(5)) register_9 (.D(rd_input), .Q(rd_output), .clk(Clock));  // open: en, clr
endmodule

module EX_MEM (
  input  [1:0] WB_input,
  input  [2:0] M_input,
  input  [31:0] PC_input,
  input  Zero_input,
  input  [31:0] ALU_res_input,
  input  [31:0] Read_Data2_input,
  input  [4:0] RegDst_input,
  input  Clock,
  output [1:0] WB_output,
  output [2:0] M_output,
  output [31:0] PC_output,
  output Zero_output,
  output [31:0] ALU_res_output,
  output [31:0] Read_Data2_output,
  output [4:0] RegDst_output
);

  Register #(.width(2)) register_1 (.D(WB_input), .Q(WB_output), .clk(Clock));  // open: en, clr
  Register #(.width(3)) register_2 (.D(M_input), .Q(M_output), .clk(Clock));  // open: en, clr
  Register #(.width(32)) register_3 (.D(PC_input), .Q(PC_output), .clk(Clock));  // open: en, clr
  Register #(.width(1)) register_4 (.D(Zero_input), .Q(Zero_output), .clk(Clock));  // open: en, clr
  Register #(.width(32)) register_5 (.D(ALU_res_input), .Q(ALU_res_output), .clk(Clock));  // open: en, clr
  Register #(.width(32)) register_6 (.D(Read_Data2_input), .Q(Read_Data2_output), .clk(Clock));  // open: en, clr
  Register #(.width(5)) register_7 (.D(RegDst_input), .Q(RegDst_output), .clk(Clock));  // open: en, clr
endmodule

module MEM_WB (
  input  [1:0] WB_input,
  input  [31:0] Read_Data_input,
  input  [31:0] Address_input,
  input  [4:0] RegDst_input,
  input  Clock,
  output [1:0] WB_output,
  output [31:0] Read_Data_output,
  output [31:0] Address_output,
  output [4:0] RegDst_output
);

  Register #(.width(2)) register_1 (.D(WB_input), .Q(WB_output), .clk(Clock));  // open: en, clr
  Register #(.width(32)) register_2 (.D(Read_Data_input), .Q(Read_Data_output), .clk(Clock));  // open: en, clr
  Register #(.width(32)) register_3 (.D(Address_input), .Q(Address_output), .clk(Clock));  // open: en, clr
  Register #(.width(5)) register_4 (.D(RegDst_input), .Q(RegDst_output), .clk(Clock));  // open: en, clr
endmodule
